# Fritzing sketch Huky_FanControl_rpm_1_1 (saved by Fritzing 0.9.3b)
circuit board: 3.81cm x 3.81cm

parts:
  ATtiny85 = attiny85 [part_number=ATtiny85 package=dip]
  100nF = Capacitor [package=cap-pth-small2]
  1µF = Electrolytic Capacitor [capacitance=1µF package="100 mil [THT, electrolytic]"]
  LM7805 = Voltage Regulator - 5V [package="TO220 [THT]"]
  100nF_2 = Capacitor [package=cap-pth-small2]
  330nF = Capacitor [package=cap-pth-small2]
  1N4002 = Diode [package=diode-1n4001]
  R2 = Resistor [tolerance=±5% resistance=10k package=THT]
  100nF_3 = Capacitor [package=cap-pth-small2]
  100nF_4 = Capacitor [package=cap-pth-small2]
  Reset = Pushbutton [package="[THT]"]
  R3 = Resistor [tolerance=±5% resistance=10k package=THT]
  J4 = screw terminal, 4 pins
  J3 = screw terminal, 4 pins
  R4 = Resistor [tolerance=±5% resistance=10k package=THT]

nets:
  N1: ATtiny85.Pin_1, R2.Pin_1, 100nF_4.1, Reset.Pin_3
  N2: ATtiny85.Pin_3, 100nF_3.2, J4.pin4, R4.Pin_1
  GND: ATtiny85.Pin_4, 100nF.2, 1µF.-, LM7805.GND, 100nF_2.1, 330nF.1, 100nF_3.1, 100nF_4.2, Reset.Pin_1, Reset.Pin_2, J4.pin2, J4.pin3, J3.pin3, R4.Pin_0
  N3: ATtiny85.Pin_5, R3.Pin_1, J3.pin2
  N4: ATtiny85.Pin_6, J3.pin1
  N5: ATtiny85.Pin_8, 100nF.1, 1µF.+, LM7805.output_voltage, 100nF_2.2, 1N4002.A, R2.Pin_0, R3.Pin_0
  12V: LM7805.input_voltage, 330nF.2, 1N4002.C, J4.pin1, J3.pin4

notes:
  Huky FanControl Rev. 1.1
